# Fritzing sketch invernadero (saved by Fritzing 0.9.3b)

parts:
  Part1 = Arduino Mega 2560 (Rev3)
  Raspberry_Pi_1 = Raspberry Pi 3 [part_number=RPI-3-V1.2]  # not connected
  RHT1 = Humidity and Temperature Sensor RHT03

nets:
  N1: Part1.GND, RHT1.GND_1
  VIN: Part1.VIN, RHT1.Vcc
  N2: Part1.D2_PWM, RHT1.Data-signal

notes:
  Conexión USB
